// Logisim project rainfall-1.circ as structural Verilog: 1 circuit, main circuit main
module main (
  input  first,
  input  second,
  input  third,
  output get_ready_to_leave,
  output avoid_getting_wet,
  output stay_home,
  output no_rain_have_fun
);

  wire and_1_out, not_1_out, or_1_out;

  and and_1 (and_1_out, second, third);
  or or_1 (or_1_out, second, third);
  not not_1 (not_1_out, or_1_out);
  and and_2 (get_ready_to_leave, first, and_1_out);
  and and_3 (avoid_getting_wet, first, or_1_out);
  and and_4 (stay_home, not_1_out, first);
  xor xor_1 (no_rain_have_fun, first, 1'b1);
endmodule
