// Logisim project rainfall-2.circ as structural Verilog: 1 circuit, main circuit main
module main (
  input  first,
  input  second,
  input  third,
  output get_ready_to_leave,
  output avoid_getting_wet,
  output stay_home,
  output no_rain_have_fun
);

  wire and_1_out, nor_1_out, xor_1_out;

  and and_1 (and_1_out, second, third);
  xor xor_1 (xor_1_out, second, third);
  nor nor_1 (nor_1_out, second, third);
  and and_2 (get_ready_to_leave, first, and_1_out);
  and and_3 (avoid_getting_wet, first, xor_1_out);
  and and_4 (stay_home, nor_1_out, first);
  xor xor_2 (no_rain_have_fun, first, 1'b1);
endmodule
